# Fritzing sketch led_capture_circuit (saved by Fritzing 0.9.2b)
breadboards: 1

parts:
  R1 = Resistor [tolerance=±5% resistance=150 package=THT]
  R2 = Resistor [tolerance=±5% resistance=10k package=THT]
  R3 = Resistor [tolerance=±5% resistance=3.3k package=THT]
  R4 = Resistor [tolerance=±5% resistance=10k package=THT]
  Q1 = NPN-Transistor [package="TO92 [THT]"]
  LED1 = smd LED [color="Green (560nm)" package="0805 [SMD]"]
  Part1 = Arduino Ethernet Shield (Rev3)
  U2 = TLP621 [package=THT]

nets:
  N1: R1.Pin_0, Part1.5V, U2.Pin_4
  N2: R1.Pin_1, U2.Pin_1
  N3: R2.Pin_0, Part1.A0, U2.Pin_3
  N4: R2.Pin_1, R4.Pin_1, Q1.E, LED1.anode, Part1.GND
  N5: R3.Pin_0, R4.Pin_0, Q1.B
  N6: R3.Pin_1, LED1.cathode
  N7: Q1.C, U2.Pin_2
